# Fritzing sketch esp32_IR_Bridge_v6 (saved by Fritzing 0.9.3b)
stripboards: 1

parts:
  LED1_IR = LED - 5mm [color="Red (633nm)" package="5 mm [THT]"]  # not connected
  LED2 = LED - 5mm [color="Red (633nm)" package="5 mm [THT]"]  # not connected
  LED3 = LED - 5mm [color="Red (633nm)" package="5 mm [THT]"]  # not connected
  Q1 = NPN-Transistor [package="TO92 [THT]"]
  J1 = female pin header, 4 pins [form="♀ (female)"]
  R2 = Resistor [tolerance=±5% resistance=100 package=THT]
  R3 = Resistor [tolerance=±5% resistance=330 package=THT]
  R4 = Resistor [tolerance=±5% resistance=330 package=THT]
  R1 = Resistor [tolerance=±5% resistance=2.2k package=THT]
  J2 = female pin header, 2 pins [form="♀ (female)"]
  J3 = female pin header, 2 pins [form="♀ (female)"]
  J4 = female pin header, 2 pins [form="♀ (female)"]

nets:
  N1: Q1.E, J1.pin2, J3.pin2
  N2: Q1.B, R1.Pin_1
  N3: Q1.C, J2.pin2, J4.pin2
  N4: J1.pin1, R2.Pin_0, R3.Pin_0
  N5: J1.pin3, R1.Pin_0
  N6: J1.pin4, R4.Pin_0
  N7: R2.Pin_1, J4.pin1
  N8: R3.Pin_1, J2.pin1
  N9: R4.Pin_1, J3.pin1

notes:
  1 at top 4 bottom, 1=+5v, 2=GND, 3=IR SIG, 4=IND LED
